# Fritzing sketch digispark_smart_light (saved by Fritzing 0.9.3b)
breadboards: 1

parts:
  Sensore_PIR_HC-SR501 = HC-SR501 Body Sensor Module
  LightSensor = PHOTOCELL [package=photocell]
  R2 = Resistor [tolerance=±5% resistance=10k package="2010 [SMD]"]
  R3 = Resistor [tolerance=±5% resistance=220 package="2010 [SMD]"]
  LED_B = smd LED [color="Blue (525nm)" package="0805 [SMD]"]
  Relay_Light = Keyes Relay [package=THT]
  BTN_INC_TIME = Pushbutton [package=THT]
  DigiSpark1 = Digispark

nets:
  VCC: Sensore_PIR_HC-SR501.VCC, LightSensor.P$1, R3.Pin_0, Relay_Light.power, BTN_INC_TIME.leg0, DigiSpark1.VCC
  N1: Sensore_PIR_HC-SR501.OUT, DigiSpark1.P3
  GND: Sensore_PIR_HC-SR501.GND, R2.Pin_1, Relay_Light.ground, DigiSpark1.GND
  N2: LightSensor.P$2, R2.Pin_0, DigiSpark1.P5
  N3: R3.Pin_1, LED_B.cathode
  N4: LED_B.anode, DigiSpark1.P1
  N5: Relay_Light.signal, DigiSpark1.P2
  N6: BTN_INC_TIME.leg1, DigiSpark1.P0

notes:
  Automatic switch on light on movement if it is dark for 2 minutes.
  Button increases lightning time by 10 minutes

custom parts:
  HC-SR501 Body Sensor Module: Pyroelectric Infrared PIR Motion Sensor Detector Module
  Keyes Relay: The Keyes 5V relay module is suitable for SCM development, home appliance control. It uses a 5V~12V TIL control signal which can control DC / AC signal.
  Digispark: The Digispark is an Attiny85 based microcontroller development board similar to the Arduino line, only cheaper, smaller, and a bit less powerful. With a whole host of shields to extend its functionality and the ability to use the familiar Arduino IDE the Digispark is a great way to jump into electronics, or perfect for when an Arduino is too big or too much.

// code stored in the sketch: uno_smart_light.ino
/*
   Uno version smart light

   Created: 4/12/2019 10:20:22 PM
   Author : Gerankin-EIS
*/

#include <avr/io.h>


#define LightSensor_PIN PB2
#define Relay_Light 5//(1<<PB0) //жёлтый
#define LED_B 3//(1<<PB1) //светодиод голубой
//#define LED_G 4//(1<<PB3) //светодиод зелёный 
#define PIR   2//датчик движения
#define calibrationTime 14 //секунд для инициализации таймера;
#define TIMEOUT_PIR 5000
#define BTN_INC 4
#define BTN_INC_TIME 5000 * 2
volatile unsigned long delayBy = 0;
volatile boolean movementOn = false;
void setup()
{
  //DDRB |= (LED_B | Relay_Light) ;
  pinMode(Relay_Light, OUTPUT);
  pinMode(LED_B, OUTPUT);
  pinMode(PIR, INPUT);
  pinMode(BTN_INC, INPUT);
  digitalWrite(BTN_INC, HIGH);
   Serial.begin(9600);
  for (int i = 0; i < calibrationTime; i++) {
    digitalWrite(LED_B, !digitalRead(LED_B));
    delay(1000);
  }
  attachInterrupt(digitalPinToInterrupt(PIR), pin_ISR, RISING );
}
void pin_ISR()
{
  movementOn = true;
  unsigned long tmp = millis() + TIMEOUT_PIR;
  if (delayBy < tmp) {
    delayBy = tmp;
    Serial.println("inc time");
  }
}
volatile bool activatedLight = false;
char btnIncCount = 0;
bool incButtonClicked = false;
void loop()
{
  if (! movementOn ) {
    return;
  }

  if (!activatedLight) {
    Serial.println("Movement");
    int photo = analogRead(0);
    Serial.println(photo);
    Serial.println(delayBy);
    if (photo > 300) {
      Serial.println("Light ON");
      digitalWrite(Relay_Light, HIGH);
      activatedLight = true;
    }
    else{
      movementOn = false;
      Serial.println("Skip movement");
    }
  }


  if (activatedLight && (millis() > delayBy)) {
    if(incButtonClicked){
      delayBy += BTN_INC_TIME;
      incButtonClicked = false;
      Serial.println("Added BTN time");
      return;
    }
    Serial.println("Time over, Light OFF");
    digitalWrite(Relay_Light, LOW);
    movementOn = false;
    delayBy = 0;
    activatedLight = false;
  }
  if(activatedLight){
    bool pressed = digitalRead(BTN_INC) == LOW;
    if( pressed && btnIncCount<5){
      btnIncCount++;
    }
    if(!pressed && btnIncCount >0){
      btnIncCount--;
    }
    
    if(btnIncCount == 5){
      incButtonClicked = true;
      btnIncCount = 0;
    }
  }
}
